// Logisim project bonkpu.circ as structural Verilog: 4 circuits, main circuit main
module main (
);

  wire AI, and_1_out, and_2_out, AO, BI, BO, button_1_out, CE, CHI, CHO, CLI, CLK, CLO, clock_1_out,
       dipswitch_1_p1, EO, FI, HLT, IE, II, MB, MHI, MLI, MS0, MU, nor_1_out, not_1_out, OC, OHI, OLI, RI,
       RO, SHO, SLO, SU, xor_1_out;
  wire [1:0] STACK_MODE;
  wire [2:0] FLAGS, nor_2_out;
  wire [3:0] MICROSTEP_q;
  wire [7:0] A_REG_q, adder_2_out, B_REG_q, MEM_dout, microcode_b_data, multiplexer_2_out, OP_REG_q,
       PROGMEM_data, stack_pointer_1_out_bus, xor_2_out;
  wire [14:0] adder_1_out;
  wire [15:0] mar_1_addr;
  wire [15:15] adder_1_out_2;

  ROM #(.addrWidth(15)) PROGMEM (.addr(adder_1_out), .data(PROGMEM_data));
  Counter #(.max('hf), .width(4)) MICROSTEP (
    .load(IE), .clk(not_1_out), .D(4'b0000), .Q(MICROSTEP_q));  // open: clr, up, count, carry
  not not_1 (not_1_out, CLK);
  Register OP_REG (.D(stack_pointer_1_out_bus), .en(II), .clk(CLK), .Q(OP_REG_q));  // open: clr
  and and_1 (and_1_out, adder_1_out_2[15], RI);
  RAM #(.addrWidth(15), .enables("line")) MEM (
    .addr(adder_1_out), .we(and_1_out), .clk(CLK), .din(stack_pointer_1_out_bus), .dout(MEM_dout));
  Comparator #(.mode("unsigned"), .width(4)) comparator_1 (.a(MICROSTEP_q), .b(4'b0000), .eq(MS0));  // open: gt, lt
  ROM #(.addrWidth(15)) microcode_a (
    .addr({FLAGS, OP_REG_q, MICROSTEP_q}), .data({IE, CE, MU, MB, SU, FI, STACK_MODE}));
  stack_pointer stack_pointer_1 (.HO(SHO), .LO(SLO), .CLK(CLK), .MODE(STACK_MODE), .out_bus(stack_pointer_1_out_bus));
  program_counter program_counter_1 (
    .CLK(CLK), .CE(CE), .LI(CLI), .HI(CHI), .HO(CHO), .LO(CLO), .bus_in(stack_pointer_1_out_bus),
    .bus_out(stack_pointer_1_out_bus));
  mar mar_1 (
    .CLK(CLK), .HI(MHI), .LI(MLI), .OHI(OHI), .OLI(OLI), .OC(OC), .bus_in(stack_pointer_1_out_bus), .U(MU),
    .addr(mar_1_addr));
  Adder #(.width(16)) adder_1 (
    .a({16{1'b0}}), .b(mar_1_addr), .out({adder_1_out_2[15], adder_1_out}), .cin(MB));  // open: cout
  Multiplexer #(.disabled("Z"), .enable("true"), .width(8)) multiplexer_1 (
    .in0(PROGMEM_data), .in1(MEM_dout), .out(stack_pointer_1_out_bus), .sel(adder_1_out_2[15]), .en(RO));
  LedBar ledbar_1 (
    .led0(stack_pointer_1_out_bus[7]), .led1(stack_pointer_1_out_bus[6]), .led2(stack_pointer_1_out_bus[5]),
    .led3(stack_pointer_1_out_bus[4]), .led4(stack_pointer_1_out_bus[3]), .led5(stack_pointer_1_out_bus[2]),
    .led6(stack_pointer_1_out_bus[1]), .led7(stack_pointer_1_out_bus[0]));
  Pull_Resistor pull_resistor_1 (.node(stack_pointer_1_out_bus));
  Register A_REG (.D(stack_pointer_1_out_bus), .en(AI), .clk(CLK), .Q(A_REG_q));  // open: clr
  assign stack_pointer_1_out_bus = AO ? A_REG_q : 8'bz;  // Controlled_Buffer controlled_buffer_1
  assign stack_pointer_1_out_bus = EO ? adder_2_out : 8'bz;  // Controlled_Buffer EO_GATE
  Register B_REG (.D(stack_pointer_1_out_bus), .en(BI), .clk(CLK), .Q(B_REG_q));  // open: clr
  LedBar #(.matrixcols(16)) ledbar_2 (
    .led0(IE), .led1(CE), .led2(MU), .led3(MB), .led4(SU), .led5(FI), .led6(STACK_MODE[1]),
    .led7(STACK_MODE[0]), .led8(microcode_b_data[7]), .led9(microcode_b_data[6]),
    .led10(microcode_b_data[5]), .led11(microcode_b_data[4]), .led12(microcode_b_data[3]),
    .led13(microcode_b_data[2]), .led14(microcode_b_data[1]), .led15(microcode_b_data[0]));
  ROM #(.addrWidth(15)) microcode_b (.addr({FLAGS, OP_REG_q, MICROSTEP_q}), .data(microcode_b_data));
  Button button_1 (.out(button_1_out));
  // DipSwitch #(.number(2)) dipswitch_1: pin names not known; wires that end beside it: dipswitch_1_p1, A_REG_q
  assign stack_pointer_1_out_bus = BO ? B_REG_q : 8'bz;  // Controlled_Buffer B_GATE
  xor xor_1 (xor_1_out, button_1_out, dipswitch_1_p1);
  // Probe on A_REG_q
  // Probe on A_REG_q
  Multiplexer #(.width(8)) multiplexer_2 (.in0({8{1'b0}}), .in1({8{1'b1}}), .out(multiplexer_2_out), .sel(SU));
  // Probe on B_REG_q
  // Probe on B_REG_q
  and and_2 (and_2_out, MS0, xor_1_out);
  assign xor_2_out = multiplexer_2_out ^ B_REG_q;  // XOR_Gate xor_2, 8 bits wide
  Clock clock_1 (.out(clock_1_out));
  nor nor_1 (nor_1_out, HLT, and_2_out);
  Adder adder_2 (.a(A_REG_q), .b(xor_2_out), .out(adder_2_out), .cin(SU), .cout(nor_2_out[2]));
  and and_3 (CLK, clock_1_out, nor_1_out);
  nor nor_2 (nor_2_out[0], adder_2_out[0], adder_2_out[1], adder_2_out[2], adder_2_out[3], adder_2_out[4], adder_2_out[5], adder_2_out[6], adder_2_out[7]);
  // Probe on adder_2_out
  // Probe on adder_2_out
  Decoder #(.enable("false"), .select(4)) decoder_1 (
    .out1(RO), .out2(AO), .out3(BO), .out4(EO), .out5(CHO), .out6(CLO), .out7(SHO), .out8(SLO), .out15(HLT),
    .sel(microcode_b_data[3:0]));  // open: out0, out9, out10, out11, out12, out13, out14
  Decoder #(.enable("false"), .select(4)) decoder_2 (
    .out1(RI), .out2(AI), .out3(BI), .out4(II), .out5(CHI), .out6(CLI), .out7(MHI), .out8(MLI), .out9(OHI),
    .out10(OLI), .out11(OC), .sel(microcode_b_data[7:4]));  // open: out0, out12, out13, out14, out15
  // Probe on microcode_b_data[7:4]
  Register #(.width(3)) FLAG_REG (
    .D({nor_2_out[2], adder_2_out[7], nor_2_out[0]}), .en(FI), .clk(CLK), .Q(FLAGS));  // open: clr
  // Probe on microcode_b_data[3:0]
  LedBar #(.matrixcols(3)) ledbar_3 (.led0(FLAGS[2]), .led1(FLAGS[1]), .led2(FLAGS[0]));

  // Notes on the sheet:
  //   contents of PROGMEM (hex, n*v repeats v):
  //   15 19 4 19 6 1b 11 0 17 17 18 19 9 1b 11 0 1d 18 18 4 5 0 d 6 0 14 2e 0 4 5 0 7 1 0 4 6 0 7 5 0 4 1
  //   0 7 6 0 4 5 0 7 1 0 1 0 7 2 0 4 2 0 a 6 0 7 2 0 4 1 0 b 1 7 1 0 10 39 0 4 2 0 1a 1a 1c
  //   contents of microcode_a (hex, n*v repeats v):
  //   0 20 c0 14*0 20 40 0 20 c0 11*0 20 40 0 20 40 70 80 9*0 20 40 0 20 40 70 0 30 80 7*0 20 40 0 20 40
  //   50 0 20 0 80 6*0 20 40 0 20 40 70 80 9*0 20 40 0 20 40 70 0 30 80 7*0 20 40 0 20 40 50 0 20 0 80 6*0
  //   20 40 0 20 40 84 10*0 20 40 0 20 40 70 0 84 8*0 20 40 0 20 40 50 0 20 0 4 80 5*0 20 40 0 20 40 8c
  //   10*0 20 40 0 20 40 70 0 8c 8*0 20 40 0 20 40 50 0 20 0 c 80 5*0 20 40 0 20 40 50 80 9*0 20 40 40 c0
  //   12*0 20 40 0 20 40 50 80 9*0 20 40 40 c0 12*0 20 40 0 20 40 50 80 9*0 20 40 40 c0 12*0 20 40 0 20 40
  //   50 80 9*0 20 40 81 13*0 20 40 83 13*0 20 40 82 13*0 20 40 0 20 83 11*0 20 40 0 20 40 0 20 83 8*0 20
  //   40 2 0 20 80 10*0 20 40 0 20 3 0 20 3 0 20 40 50 80 0 0 0 20 40 2 0 20 2 0 20 0 40 c0 5*0 20 40 80
  //   13*0 20 c0 14*0 20 c0 14*0 20 c0 14*0 20 c0 14*0 20 c0 14*0 20 c0 14*0 20 c0 14*0 20 c0 14*0 20 c0
  //   14*0 20 c0 14*0 20 c0 14*0 20 c0 14*0 20 c0 14*0 20 c0 14*0 20 c0 14*0 20 c0 14*0 20 c0 14*0 20 c0
  //   14*0 20 c0 14*0 20 c0 14*0 20 c0 14*0 20 c0 14*0 20 c0 14*0 20 c0 14*0 20 c0 14*0 20 c0 14*0 20 c0
  //   14*0 20 c0 14*0 20 c0 14*0 20 c0 14*0 20 c0 14*0 20 c0 14*0 20 c0 14*0 20 c0 14*0 20 c0 14*0 20 c0
  //   14*0 20 c0 14*0 20 c0 14*0 20 c0 14*0 20 c0 14*0 20 c0 14*0 20 c0 14*0 20 c0 14*0 20 c0 14*0 20 c0
  //   14*0 20 c0 14*0 20 c0 14*0 20 c0 14*0 20 c0 14*0 20 c0 14*0 20 c0 14*0 20 c0 14*0 20 c0 14*0 20 c0
  //   14*0 20 c0 14*0 20 c0 14*0 20 c0 14*0 20 c0 14*0 20 c0 14*0 20 c0 14*0 20 c0 14*0 20 c0 14*0 20 c0
  //   14*0 20 c0 14*0 20 c0 14*0 20 c0 14*0 20 c0 14*0 20 c0 14*0 20 c0 14*0 20 c0 14*0 20 c0 14*0 20 c0
  //   14*0 20 c0 14*0 20 c0 14*0 20 c0 14*0 20 c0 14*0 20 c0 14*0 20 c0 14*0 20 c0 14*0 20 c0 14*0 20 c0
  //   14*0 20 c0 14*0 20 c0 14*0 20 c0 14*0 20 c0 14*0 20 c0 14*0 20 c0 14*0 20 c0 14*0 20 c0 14*0 20 c0
  //   14*0 20 c0 14*0 20 c0 14*0 20 c0 14*0 20 c0 14*0 20 c0 14*0 20 c0 14*0 20 c0 14*0 20 c0 14*0 20 c0
  //   14*0 20 c0 14*0 20 c0 14*0 20 c0 14*0 20 c0 14*0 20 c0 14*0 20 c0 14*0 20 c0 14*0 20 c0 14*0 20 c0
  //   14*0 20 c0 14*0 20 c0 14*0 20 c0 14*0 20 c0 14*0 20 c0 14*0 20 c0 14*0 20 c0 14*0 20 c0 14*0 20 c0
  //   14*0 20 c0 14*0 20 c0 14*0 20 c0 14*0 20 c0 14*0 20 c0 14*0 20 c0 14*0 20 c0 14*0 20 c0 14*0 20 c0
  //   14*0 20 c0 14*0 20 c0 14*0 20 c0 14*0 20 c0 14*0 20 c0 14*0 20 c0 14*0 20 c0 14*0 20 c0 14*0 20 c0
  //   14*0 20 c0 14*0 20 c0 14*0 20 c0 14*0 20 c0 14*0 20 c0 14*0 20 c0 14*0 20 c0 14*0 20 c0 14*0 20 c0
  //   14*0 20 c0 14*0 20 c0 14*0 20 c0 14*0 20 c0 14*0 20 c0 14*0 20 c0 14*0 20 c0 14*0 20 c0 14*0 20 c0
  //   14*0 20 c0 14*0 20 c0 14*0 20 c0 14*0 20 c0 14*0 20 c0 14*0 20 c0 14*0 20 c0 14*0 20 c0 14*0 20 c0
  //   14*0 20 c0 14*0 20 c0 14*0 20 c0 14*0 20 c0 14*0 20 c0 14*0 20 c0 14*0 20 c0 14*0 20 c0 14*0 20 c0
  //   14*0 20 c0 14*0 20 c0 14*0 20 c0 14*0 20 c0 14*0 20 c0 14*0 20 c0 14*0 20 c0 14*0 20 c0 14*0 20 c0
  //   14*0 20 c0 14*0 20 c0 14*0 20 c0 14*0 20 c0 14*0 20 c0 14*0 20 c0 14*0 20 c0 14*0 20 c0 14*0 20 c0
  //   14*0 20 c0 14*0 20 c0 14*0 20 c0 14*0 20 c0 14*0 20 c0 14*0 20 c0 14*0 20 c0 14*0 20 c0 14*0 20 c0
  //   14*0 20 c0 14*0 20 c0 14*0 20 c0 14*0 20 c0 14*0 20 c0 14*0 20 c0 14*0 20 c0 14*0 20 c0 14*0 20 c0
  //   14*0 20 c0 14*0 20 c0 14*0 20 c0 14*0 20 c0 14*0 20 c0 14*0 20 c0 14*0 20 c0 14*0 20 c0 14*0 20 c0
  //   14*0 20 c0 14*0 20 c0 14*0 20 c0 14*0 20 c0 14*0 20 c0 14*0 20 c0 14*0 20 c0 14*0 20 c0 14*0 20 c0
  //   14*0 20 c0 14*0 20 c0 14*0 20 40 0 20 c0 11*0 20 40 0 20 40 70 80 9*0 20 40 0 20 40 70 0 30 80 7*0
  //   20 40 0 20 40 50 0 20 0 80 6*0 20 40 0 20 40 70 80 9*0 20 40 0 20 40 70 0 30 80 7*0 20 40 0 20 40 50
  //   0 20 0 80 6*0 20 40 0 20 40 84 10*0 20 40 0 20 40 70 0 84 8*0 20 40 0 20 40 50 0 20 0 4 80 5*0 20 40
  //   0 20 40 8c 10*0 20 40 0 20 40 70 0 8c 8*0 20 40 0 20 40 50 0 20 0 c 80 5*0 20 40 0 20 40 50 80 9*0
  //   20 40 0 20 40 50 80 9*0 20 40 40 c0 12*0 20 40 40 c0 12*0 20 40 0 20 40 50 80 9*0 20 40 40 c0 12*0
  //   20 40 0 20 40 50 80 9*0 20 40 81 13*0 20 40 83 13*0 20 40 82 13*0 20 40 0 20 83 11*0 20 40 0 20 40 0
  //   20 83 8*0 20 40 2 0 20 80 10*0 20 40 0 20 3 0 20 3 0 20 40 50 80 0 0 0 20 40 2 0 20 2 0 20 0 40 c0
  //   5*0 20 40 80 13*0 20 c0 14*0 20 c0 14*0 20 c0 14*0 20 c0 14*0 20 c0 14*0 20 c0 14*0 20 c0 14*0 20 c0
  //   14*0 20 c0 14*0 20 c0 14*0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
  //   contents of microcode_b (hex, n*v repeats v):
  //   86 75 41 13*0 86 75 41 86 75 21 10*0 86 75 41 86 75 81 71 21 8*0 86 75 41 86 75 81 71 81 71 21 6*0
  //   86 75 41 86 75 a1 91 88 77 21 b0 5*0 86 75 41 86 75 81 71 12 8*0 86 75 41 86 75 81 71 81 71 12 6*0
  //   86 75 41 86 75 a1 91 88 77 12 b0 5*0 86 75 41 86 75 31 24 9*0 86 75 41 86 75 81 71 31 24 7*0 86 75
  //   41 86 75 a1 91 88 77 31 24 b0 4*0 86 75 41 86 75 31 24 9*0 86 75 41 86 75 81 71 31 24 7*0 86 75 41
  //   86 75 a1 91 88 77 31 24 b0 4*0 86 75 41 86 75 31 51 63 8*0 86 75 41 13*0 86 75 41 86 75 31 51 63 8*0
  //   86 75 41 13*0 86 75 41 86 75 31 51 63 8*0 86 75 41 13*0 86 75 41 86 75 31 51 63 8*0 86 75 41 13*0 86
  //   75 41 13*0 86 75 41 13*0 86 75 41 88 77 12 10*0 86 75 41 86 75 31 88 77 13 7*0 86 75 41 0 88 77 21
  //   9*0 86 75 41 88 77 15 88 77 16 86 75 31 51 63 0 0 86 75 41 0 88 77 61 88 77 51 6*0 86 75 41 f 12*0
  //   86 75 41 13*0 86 75 41 13*0 86 75 41 13*0 86 75 41 13*0 86 75 41 13*0 86 75 41 13*0 86 75 41 13*0 86
  //   75 41 13*0 86 75 41 13*0 86 75 41 13*0 86 75 41 13*0 86 75 41 13*0 86 75 41 13*0 86 75 41 13*0 86 75
  //   41 13*0 86 75 41 13*0 86 75 41 13*0 86 75 41 13*0 86 75 41 13*0 86 75 41 13*0 86 75 41 13*0 86 75 41
  //   13*0 86 75 41 13*0 86 75 41 13*0 86 75 41 13*0 86 75 41 13*0 86 75 41 13*0 86 75 41 13*0 86 75 41
  //   13*0 86 75 41 13*0 86 75 41 13*0 86 75 41 13*0 86 75 41 13*0 86 75 41 13*0 86 75 41 13*0 86 75 41
  //   13*0 86 75 41 13*0 86 75 41 13*0 86 75 41 13*0 86 75 41 13*0 86 75 41 13*0 86 75 41 13*0 86 75 41
  //   13*0 86 75 41 13*0 86 75 41 13*0 86 75 41 13*0 86 75 41 13*0 86 75 41 13*0 86 75 41 13*0 86 75 41
  //   13*0 86 75 41 13*0 86 75 41 13*0 86 75 41 13*0 86 75 41 13*0 86 75 41 13*0 86 75 41 13*0 86 75 41
  //   13*0 86 75 41 13*0 86 75 41 13*0 86 75 41 13*0 86 75 41 13*0 86 75 41 13*0 86 75 41 13*0 86 75 41
  //   13*0 86 75 41 13*0 86 75 41 13*0 86 75 41 13*0 86 75 41 13*0 86 75 41 13*0 86 75 41 13*0 86 75 41
  //   13*0 86 75 41 13*0 86 75 41 13*0 86 75 41 13*0 86 75 41 13*0 86 75 41 13*0 86 75 41 13*0 86 75 41
  //   13*0 86 75 41 13*0 86 75 41 13*0 86 75 41 13*0 86 75 41 13*0 86 75 41 13*0 86 75 41 13*0 86 75 41
  //   13*0 86 75 41 13*0 86 75 41 13*0 86 75 41 13*0 86 75 41 13*0 86 75 41 13*0 86 75 41 13*0 86 75 41
  //   13*0 86 75 41 13*0 86 75 41 13*0 86 75 41 13*0 86 75 41 13*0 86 75 41 13*0 86 75 41 13*0 86 75 41
  //   13*0 86 75 41 13*0 86 75 41 13*0 86 75 41 13*0 86 75 41 13*0 86 75 41 13*0 86 75 41 13*0 86 75 41
  //   13*0 86 75 41 13*0 86 75 41 13*0 86 75 41 13*0 86 75 41 13*0 86 75 41 13*0 86 75 41 13*0 86 75 41
  //   13*0 86 75 41 13*0 86 75 41 13*0 86 75 41 13*0 86 75 41 13*0 86 75 41 13*0 86 75 41 13*0 86 75 41
  //   13*0 86 75 41 13*0 86 75 41 13*0 86 75 41 13*0 86 75 41 13*0 86 75 41 13*0 86 75 41 13*0 86 75 41
  //   13*0 86 75 41 13*0 86 75 41 13*0 86 75 41 13*0 86 75 41 13*0 86 75 41 13*0 86 75 41 13*0 86 75 41
  //   13*0 86 75 41 13*0 86 75 41 13*0 86 75 41 13*0 86 75 41 13*0 86 75 41 13*0 86 75 41 13*0 86 75 41
  //   13*0 86 75 41 13*0 86 75 41 13*0 86 75 41 13*0 86 75 41 13*0 86 75 41 13*0 86 75 41 13*0 86 75 41
  //   13*0 86 75 41 13*0 86 75 41 13*0 86 75 41 13*0 86 75 41 13*0 86 75 41 13*0 86 75 41 13*0 86 75 41
  //   13*0 86 75 41 13*0 86 75 41 13*0 86 75 41 13*0 86 75 41 13*0 86 75 41 13*0 86 75 41 13*0 86 75 41
  //   13*0 86 75 41 13*0 86 75 41 13*0 86 75 41 13*0 86 75 41 13*0 86 75 41 13*0 86 75 41 13*0 86 75 41
  //   13*0 86 75 41 13*0 86 75 41 13*0 86 75 41 13*0 86 75 41 13*0 86 75 41 13*0 86 75 41 13*0 86 75 41
  //   13*0 86 75 41 13*0 86 75 41 13*0 86 75 41 13*0 86 75 41 13*0 86 75 41 13*0 86 75 41 13*0 86 75 41
  //   13*0 86 75 41 13*0 86 75 41 13*0 86 75 41 13*0 86 75 41 13*0 86 75 41 13*0 86 75 41 13*0 86 75 41
  //   13*0 86 75 41 13*0 86 75 41 13*0 86 75 41 13*0 86 75 41 13*0 86 75 41 13*0 86 75 41 13*0 86 75 41
  //   13*0 86 75 41 13*0 86 75 41 13*0 86 75 41 13*0 86 75 41 13*0 86 75 41 13*0 86 75 41 13*0 86 75 41
  //   13*0 86 75 41 13*0 86 75 41 13*0 86 75 41 13*0 86 75 41 13*0 86 75 41 13*0 86 75 41 13*0 86 75 41
  //   13*0 86 75 41 13*0 86 75 41 13*0 86 75 41 13*0 86 75 41 13*0 86 75 41 13*0 86 75 41 13*0 86 75 41
  //   13*0 86 75 41 13*0 86 75 41 13*0 86 75 41 13*0 86 75 41 13*0 86 75 41 13*0 86 75 41 13*0 86 75 41
  //   13*0 86 75 41 13*0 86 75 41 13*0 86 75 41 86 75 21 10*0 86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
endmodule

module stack_pointer (
  input  CLK,
  input  [1:0] MODE,
  input  HO,
  input  LO,
  output [7:0] out_bus
);

  wire and_1_out, counter_2_carry, decoder_1_out0, decoder_1_out1, decoder_1_out2, decoder_1_out3, or_1_out,
       or_2_out, or_3_out;
  wire [7:0] counter_1_q, counter_2_q;

  // NoConnect on decoder_1_out0
  Decoder #(.enable("false"), .select(2)) decoder_1 (
    .out0(decoder_1_out0), .out1(decoder_1_out1), .out2(decoder_1_out2), .out3(decoder_1_out3), .sel(MODE));
  LED DEC (.in(decoder_1_out3));
  LED LOAD (.in(decoder_1_out1));
  LED INC (.in(decoder_1_out2));
  or or_1 (or_1_out, decoder_1_out2, decoder_1_out3);
  and and_1 (and_1_out, or_1_out, counter_2_carry);
  or or_2 (or_2_out, decoder_1_out1, decoder_1_out2, decoder_1_out3);
  or or_3 (or_3_out, decoder_1_out1, and_1_out);
  Counter counter_1 (
    .load(decoder_1_out1), .up(decoder_1_out2), .count(or_3_out), .clk(CLK), .D({8{1'b1}}), .Q(counter_1_q));  // open: clr, carry
  Counter counter_2 (
    .load(decoder_1_out1), .up(decoder_1_out2), .count(or_2_out), .clk(CLK), .D({8{1'b1}}),
    .carry(counter_2_carry), .Q(counter_2_q));  // open: clr
  assign out_bus = HO ? counter_1_q : 8'bz;  // Controlled_Buffer controlled_buffer_1
  assign out_bus = LO ? counter_2_q : 8'bz;  // Controlled_Buffer controlled_buffer_2
endmodule

module program_counter (
  input  CLK,
  input  CE,
  input  HI,
  input  HO,
  input  LI,
  input  LO,
  input  [7:0] bus_in,
  output [7:0] bus_out
);

  wire and_1_out, CL_carry, or_1_out, or_2_out;
  wire [7:0] CH_q, CL_q;

  and and_1 (and_1_out, CE, CL_carry);
  or or_1 (or_1_out, LI, CE);
  or or_2 (or_2_out, HI, and_1_out);
  Counter CH (.load(HI), .count(or_2_out), .clk(CLK), .D(bus_in), .Q(CH_q));  // open: clr, up, carry
  Counter CL (.load(LI), .count(or_1_out), .clk(CLK), .D(bus_in), .carry(CL_carry), .Q(CL_q));  // open: clr, up
  assign bus_out = HO ? CH_q : 8'bz;  // Controlled_Buffer controlled_buffer_1
  assign bus_out = LO ? CL_q : 8'bz;  // Controlled_Buffer controlled_buffer_2
endmodule

module mar (
  input  CLK,
  input  HI,
  input  LI,
  input  [7:0] bus_in,
  input  OHI,
  input  OLI,
  input  U,
  input  OC,
  output [15:0] addr
);

  wire [7:0] MARH_q, MARL_q, OH_q, OL_q;
  wire [15:0] adder_1_out;

  Register MARH (.D(bus_in), .en(HI), .clk(CLK), .Q(MARH_q));  // open: clr
  Register OH (.D(bus_in), .en(OHI), .clk(CLK), .Q(OH_q), .clr(OC));
  Register MARL (.D(bus_in), .en(LI), .clk(CLK), .Q(MARL_q));  // open: clr
  Register OL (.D(bus_in), .en(OLI), .clk(CLK), .Q(OL_q), .clr(OC));
  Adder #(.width(16)) adder_1 (.a({MARH_q, MARL_q}), .b({OH_q, OL_q}), .out(adder_1_out));  // open: cin, cout
  Register #(.trigger("high"), .width(16)) MARV (.D(adder_1_out), .en(U), .clk(CLK), .Q(addr));  // open: clr
endmodule
